// Logisim project proj.circ as structural Verilog: 29 circuits, main circuit main
module main (
);

  wire acalu_ctrl_1_clr, acalu_ctrl_1_inc, acalu_ctrl_1_load, ar_ctrl_1_clr, ar_ctrl_1_inc, ar_ctrl_1_load,
       CLK, clock_1_out, dr_ctrl_1_inc, dr_ctrl_1_load, E, E_out, FGI, FGO, I, IEN, ir_ctrl_1_load,
       memory_ctrl_1_read, memory_ctrl_1_write, outr_ctrl_1_load, p, pc_ctrl_1_clr, pc_ctrl_1_inc,
       pc_ctrl_1_load, R, r_t, Start, tr_ctrl_1_load;
  wire [2:0] acalu_ctrl_1_order, bus_ctrl_1_s;
  wire [7:0] convert_16_to_8_1_out_2, IRD, register_8_bit_1_out_4, register_8_bit_2_out_4;
  wire [11:0] convert_16_to_12_1_out_2, convert_16_to_12_2_out_2, counter_12_bit_1_out_6,
       counter_12_bit_2_out_6, IRB;
  wire [15:0] AC, alu_1_output, bus_1_output, counter_16_bit_1_out_6, IR, ram_1_data,
       register_16_bit_2_out_4, SCD;

  // Probe on bus_1_output
  Convert_16_To_12 convert_16_to_12_1 (.in_1(bus_1_output), .out_2(convert_16_to_12_1_out_2));
  Convert_16_To_12 convert_16_to_12_2 (.in_1(bus_1_output), .out_2(convert_16_to_12_2_out_2));
  Convert_16_to_8 convert_16_to_8_1 (.in_1(bus_1_output), .out_2(convert_16_to_8_1_out_2));
  Register_8_Bit register_8_bit_1 (.out_4(register_8_bit_1_out_4));  // open: in_1, Load, CLK
  ACALU_CTRL acalu_ctrl_1 (
    .IRD(IRD), .SCD(SCD), .r(r_t), .p(p), .IRB(IRB), .CLR(acalu_ctrl_1_clr), .INC(acalu_ctrl_1_inc),
    .Load(acalu_ctrl_1_load), .Order(acalu_ctrl_1_order));
  // Probe on acalu_ctrl_1_order
  ALU alu_1 (
    .DR(counter_16_bit_1_out_6), .AC(AC), .E_in(E), .INPR(register_8_bit_1_out_4),
    .Order(acalu_ctrl_1_order), .Enable(acalu_ctrl_1_load), .Output(alu_1_output), .E_Out(E_out));
  Memory_CTRL memory_ctrl_1 (
    .I(I), .R(R), .IRD(IRD), .SCD(SCD), .Read(memory_ctrl_1_read), .Write(memory_ctrl_1_write));
  AR_CTRL ar_ctrl_1 (
    .I(I), .R(R), .IRD(IRD), .SCD(SCD), .Load(ar_ctrl_1_load), .INC(ar_ctrl_1_inc), .CLR(ar_ctrl_1_clr));
  PC_CTRL pc_ctrl_1 (
    .AC(AC), .I(I), .R(R), .p(p), .IRD(IRD), .SCD(SCD), .r_2(r_t), .in_8(E), .DR(counter_16_bit_1_out_6),
    .FGI(FGI), .FGO(FGO), .IRB(IRB), .CLR(pc_ctrl_1_clr), .INC(pc_ctrl_1_inc), .Load(pc_ctrl_1_load));
  Counter_16_Bit counter_16_bit_1 (
    .out_6(counter_16_bit_1_out_6), .INC(dr_ctrl_1_inc), .CLK(CLK), .in_2(bus_1_output), .CLR(1'b0),
    .Load(dr_ctrl_1_load));
  DR_CTRL dr_ctrl_1 (.IRD(IRD), .SCD(SCD), .Load(dr_ctrl_1_load), .INC(dr_ctrl_1_inc));
  Counter_16_Bit counter_16_bit_2 (
    .out_6(AC), .INC(acalu_ctrl_1_inc), .CLK(CLK), .in_2(alu_1_output), .CLR(acalu_ctrl_1_clr),
    .Load(acalu_ctrl_1_load));
  IR_CTRL ir_ctrl_1 (.R(R), .SCD(SCD), .Load(ir_ctrl_1_load));
  TR_CTRL tr_ctrl_1 (.R(R), .SCD(SCD), .Load(tr_ctrl_1_load));
  OUTR_CTRL outr_ctrl_1 (.p(p), .IRB(IRB), .Load(outr_ctrl_1_load));
  RAM #(.addrWidth(12), .dataWidth(16), .bus("separate")) ram_1 (
    .addr(counter_12_bit_1_out_6), .din(bus_1_output), .data(ram_1_data), .str(memory_ctrl_1_write),
    .clk(CLK), .ld(memory_ctrl_1_read));  // open: sel, clr
  Counter_12_Bit counter_12_bit_1 (
    .in_2(convert_16_to_12_1_out_2), .INC(ar_ctrl_1_inc), .CLK(CLK), .CLR(ar_ctrl_1_clr),
    .out_6(counter_12_bit_1_out_6), .Load(ar_ctrl_1_load));
  Counter_12_Bit counter_12_bit_2 (
    .in_2(convert_16_to_12_2_out_2), .INC(pc_ctrl_1_inc), .CLK(CLK), .CLR(pc_ctrl_1_clr),
    .out_6(counter_12_bit_2_out_6), .Load(pc_ctrl_1_load));
  Register_16_Bit register_16_bit_1 (.in_1(bus_1_output), .Load(ir_ctrl_1_load), .CLK(CLK), .out_4(IR));
  Register_16_Bit register_16_bit_2 (
    .in_1(bus_1_output), .Load(tr_ctrl_1_load), .CLK(CLK), .out_4(register_16_bit_2_out_4));
  Register_8_Bit register_8_bit_2 (
    .in_1(convert_16_to_8_1_out_2), .Load(outr_ctrl_1_load), .CLK(CLK), .out_4(register_8_bit_2_out_4));
  // Probe on register_8_bit_2_out_4
  // Probe on bus_ctrl_1_s
  // Probe on counter_12_bit_1_out_6
  // Probe on counter_12_bit_2_out_6
  // Probe on counter_16_bit_1_out_6
  // Probe on AC
  // Probe on IR
  // Probe on register_16_bit_2_out_4
  BUS_CTRL bus_ctrl_1 (.I(I), .R(R), .p(p), .SCD(SCD), .IRD(IRD), .IRB(IRB), .S(bus_ctrl_1_s));
  BUS bus_1 (
    .DR(counter_16_bit_1_out_6), .AC(AC), .IR(IR), .S(bus_ctrl_1_s), .TR(register_16_bit_2_out_4),
    .RAM(ram_1_data), .AR(counter_12_bit_1_out_6), .PC(counter_12_bit_2_out_6), .Output(bus_1_output));
  R r_1 (.SCD(SCD), .FGI(FGI), .FGO(FGO), .IEN(IEN), .R(R), .Clock(CLK));
  FGI fgi_1 (.p(p), .IRB(IRB), .FGI(FGI), .Clock(CLK));  // open: _1
  FGO fgo_1 (.p(p), .IRB(IRB), .FGO(FGO), .Clock(CLK));  // open: _1
  IEN ien_1 (.R(R), .p(p), .IRB(IRB), .SCD(SCD), .IEN(IEN), .Clock(CLK));
  Start start_1 (.r(r_t), .IRB(IRB), .Start(Start), .Clock(CLK));
  SCD scd_1 (.R(R), .p(p), .IRD(IRD), .SCD(SCD), .CLK(CLK), .Start(Start), .r_2(r_t));
  // Probe on IRB
  Options options_1 (.IR(IR), .IRB(IRB), .IRD(IRD), .I(I), .SCD(SCD), .r(r_t), .p(p));
  E e_1 (.r(r_t), .IRD(IRD), .SCD(SCD), .IRB(IRB), .AC(AC), .E(E), .E_Out(E_out), .CLK(CLK));
  Clock clock_1 (.out(clock_1_out));
  // Probe on SCD
  // Probe on E
  and and_1 (CLK, clock_1_out, Start);

  // Notes on the sheet:
  //   INPR
  //   AR
  //   PC
  //   DR
  //   AC
  //   IR
  //   TR
  //   OUTR
endmodule

module Memory_CTRL (
  input  I,
  input  R,
  input  [7:0] IRD,
  input  [15:0] SCD,
  output Read,
  output Write
);

  wire and_1_out, and_2_out, and_3_out, and_4_out, and_5_out, and_6_out, and_7_out, not_1_out, not_2_out,
       or_1_out;

  not not_1 (not_1_out, R);
  and and_1 (and_1_out, not_1_out, SCD[1]);
  and and_2 (and_2_out, R, SCD[1]);
  and and_3 (and_3_out, IRD[3], SCD[4]);
  and and_4 (and_4_out, SCD[4], IRD[5]);
  and and_5 (and_5_out, IRD[6], SCD[6]);
  not not_2 (not_2_out, IRD[7]);
  and and_6 (and_6_out, not_2_out, I, SCD[3]);
  or or_1 (or_1_out, IRD[0], IRD[1], IRD[2], IRD[6]);
  and and_7 (and_7_out, SCD[4], or_1_out);
  or or_2 (Read, and_1_out, and_6_out, and_7_out);
  or or_3 (Write, and_2_out, and_3_out, and_4_out, and_5_out);

  // Other names for the same wires on the sheet: D0 = IRD[0]; D1 = IRD[1]; D2 = IRD[2]; D3 = IRD[3]; D5 = IRD[5];
  //   D6 = IRD[6]; D7 = IRD[7]; T1 = SCD[1]; T3 = SCD[3]; T4 = SCD[4]; T6 = SCD[6]
endmodule

module Counter_12_Bit (
  input  Load,
  input  [11:0] in_2,
  input  INC,
  input  CLK,
  input  CLR,
  output [11:0] out_6
);

  Counter #(.width(12), .max('hfff)) counter_1 (
    .load(Load), .D(in_2), .count(INC), .Q(out_6), .clk(CLK), .clr(CLR));  // open: carry
endmodule

module AR_CTRL (
  input  I,
  input  R,
  input  [7:0] IRD,
  input  [15:0] SCD,
  output Load,
  output INC,
  output CLR
);

  wire and_1_out, and_2_out, and_3_out, not_1_out, not_2_out, not_3_out;

  not not_1 (not_1_out, R);
  not not_2 (not_2_out, R);
  and and_1 (and_1_out, not_2_out, SCD[2]);
  not not_3 (not_3_out, IRD[7]);
  and and_2 (and_2_out, not_1_out, SCD[0]);
  and and_3 (and_3_out, not_3_out, I, SCD[3]);
  or or_1 (Load, and_2_out, and_1_out, and_3_out);
  and and_4 (INC, IRD[5], SCD[4]);
  and and_5 (CLR, SCD[0], R);

  // Other names for the same wires on the sheet: D5 = IRD[5]; D7 = IRD[7]; T0 = SCD[0]; T2 = SCD[2]; T3 = SCD[3];
  //   T4 = SCD[4]
endmodule

module Counter_16_Bit (
  input  Load,
  input  [15:0] in_2,
  input  INC,
  input  CLK,
  input  CLR,
  output [15:0] out_6
);

  Counter #(.width(16), .max('hffff)) counter_1 (
    .load(Load), .D(in_2), .count(INC), .Q(out_6), .clk(CLK), .clr(CLR));  // open: carry
endmodule

module PC_CTRL (
  input  [15:0] AC,
  input  I,
  input  R,
  input  p,
  input  [7:0] IRD,
  input  [15:0] SCD,
  input  r_2,
  input  in_8,
  input  [15:0] DR,
  input  FGI,
  input  FGO,
  input  [11:0] IRB,
  output CLR,
  output INC,
  output Load
);

  wire and_2_out, and_3_out, and_4_out, and_5_out, and_6_out, and_7_out, and_8_out, and_9_out, and_10_out,
       and_11_out, DR_0, not_1_out, not_2_out, not_3_out;

  and and_1 (CLR, R, SCD[1]);
  and and_2 (and_2_out, IRB[4], r_2, not_1_out);
  not not_1 (not_1_out, AC[15]);
  and and_3 (and_3_out, AC[15], r_2, IRB[3]);
  not not_2 (not_2_out, in_8);
  and and_4 (and_4_out, IRD[5], SCD[5]);
  and and_5 (and_5_out, not_2_out, IRB[0], r_2);
  and and_6 (and_6_out, IRD[4], SCD[4]);
  or or_1 (Load, and_6_out, and_4_out);
  not not_3 (not_3_out, R);
  and and_7 (and_7_out, IRB[9], p, FGI);
  and and_8 (and_8_out, p, IRB[8], FGO);
  and and_9 (and_9_out, not_3_out, SCD[1]);
  and and_10 (and_10_out, R, SCD[2]);
  and and_11 (and_11_out, IRD[6], SCD[6], DR_0);
  or or_2 (INC, and_9_out, and_10_out, and_11_out, and_2_out, and_3_out, and_5_out, and_7_out, and_8_out);
  IsZero iszero_1 (.Input(DR), .IsZero(DR_0));
  IsZero iszero_2 (.Input(AC), .IsZero(DR_0));

  // Other names for the same wires on the sheet: E = in_8; B1 = IRB[0]; B3 = IRB[3]; B4 = IRB[4]; B8 = IRB[8];
  //   B9 = IRB[9]; D4 = IRD[4]; D5 = IRD[5]; D6 = IRD[6]; r_t = r_2; T1 = SCD[1]; T2 = SCD[2]; T3 = SCD[3];
  //   T4 = SCD[4]; T5 = SCD[5]; T6 = SCD[6]
endmodule

module IsZero (
  input  [15:0] Input,
  output IsZero
);

  nor nor_1 (IsZero, Input[0], Input[1], Input[2], Input[3], Input[4], Input[5], Input[6], Input[7], Input[9], Input[10], Input[11], Input[12], Input[13], Input[14], Input[15], Input[8]);
endmodule

module DR_CTRL (
  input  [7:0] IRD,
  input  [15:0] SCD,
  output Load,
  output INC
);

  wire or_1_out;

  or or_1 (or_1_out, IRD[0], IRD[1], IRD[2], IRD[6]);
  and and_1 (INC, IRD[6], SCD[5]);
  and and_2 (Load, or_1_out, SCD[4]);

  // Other names for the same wires on the sheet: D0 = IRD[0]; D1 = IRD[1]; D2 = IRD[2]; D5 = IRD[5]; D6 = IRD[6];
  //   T4 = SCD[4]; T5 = SCD[5]
endmodule

module ALU (
  input  [15:0] DR,
  input  [15:0] AC,
  input  E_in,
  input  [7:0] INPR,
  input  [2:0] Order,
  input  Enable,
  output E_Out,
  output [15:0] Output
);

  wire [0:0] shifter_2_out;
  wire [14:0] SHR;
  wire [15:0] ADD, AND, Comp;
  wire [15:1] SHL;
  wire [15:15] shifter_1_out;

  assign AND = AC & DR;  // AND_Gate and_1, 16 bits wide
  Adder #(.width(16)) adder_1 (.a(AC), .b(DR), .out(ADD), .cin(E_in), .cout(E_Out));
  assign Comp = ~AC;  // NOT_Gate not_1, 16 bits wide
  Shifter #(.width(16), .shift("lr")) shifter_1 (.in(AC), .\dist (4'b0001), .out({shifter_1_out[15], SHR}));
  Shifter #(.width(16)) shifter_2 (.in(AC), .\dist (4'b0001), .out({SHL, shifter_2_out[0]}));
  Multiplexer #(.select(3), .width(16)) multiplexer_1 (
    .in0(AND), .in1(ADD), .in2(DR), .in3({{8{1'b0}}, INPR}), .in4(Comp), .in5({E_in, SHR}),
    .in6({SHL, E_in}), .out(Output), .sel(Order), .en(Enable));  // open: in7

  // Other names for the same wires on the sheet: INPR_t[7:0] = INPR; SHL[0] = E_in; SHR[15] = E_in
endmodule

module Register_8_Bit (
  input  [7:0] in_1,
  input  Load,
  input  CLK,
  output [7:0] out_4
);

  Register register_1 (.D(in_1), .en(Load), .Q(out_4), .clk(CLK));  // open: clr
endmodule

module ACALU_CTRL (
  input  [7:0] IRD,
  input  [15:0] SCD,
  input  r,
  input  p,
  input  [11:0] IRB,
  output [2:0] Order,
  output Load,
  output CLR,
  output INC
);

  wire ADD, AND, Comp, DR, INPR, SHL, SHR;

  and and_1 (AND, IRD[0], SCD[5]);
  and and_2 (ADD, IRD[1], SCD[5]);
  and and_3 (DR, IRD[2], SCD[5]);
  and and_4 (INPR, p, IRB[11]);
  and and_5 (Comp, r, IRB[9]);
  and and_6 (SHR, r, IRB[7]);
  and and_7 (SHL, r, IRB[6]);
  and and_8 (CLR, r, IRB[11]);
  and and_9 (INC, r, IRB[5]);
  Priority_Encoder priority_encoder_1 (
    .in0(AND), .in1(ADD), .in2(DR), .in3(INPR), .in4(Comp), .in5(SHR), .in6(SHL), .out(Order), .gs(Load));  // open: in7, en_in, en_out

  // Other names for the same wires on the sheet: B5 = IRB[5]; B6 = IRB[6]; B7 = IRB[7]; B9 = IRB[9]; B11 = IRB[11];
  //   D0 = IRD[0]; D1 = IRD[1]; D2 = IRD[2]; T5 = SCD[5]
endmodule

module Register_16_Bit (
  input  [15:0] in_1,
  input  Load,
  input  CLK,
  output [15:0] out_4
);

  Register #(.width(16)) register_1 (.D(in_1), .en(Load), .Q(out_4), .clk(CLK));  // open: clr
endmodule

module IR_CTRL (
  input  R,
  input  [15:0] SCD,
  output Load
);

  wire not_1_out;

  not not_1 (not_1_out, R);
  and and_1 (Load, not_1_out, SCD[1]);

  // Other names for the same wires on the sheet: T1 = SCD[1]
endmodule

module TR_CTRL (
  input  R,
  input  [15:0] SCD,
  output Load
);

  and and_1 (Load, R, SCD[0]);

  // Other names for the same wires on the sheet: T0 = SCD[0]
endmodule

module OUTR_CTRL (
  input  p,
  input  [11:0] IRB,
  output Load
);

  and and_1 (Load, p, IRB[10]);

  // Other names for the same wires on the sheet: B10 = IRB[10]
endmodule

module BUS (
  input  [15:0] RAM,
  input  [15:0] DR,
  input  [15:0] AC,
  input  [15:0] IR,
  input  [2:0] S,
  input  [15:0] TR,
  input  [11:0] AR,
  input  [11:0] PC,
  output [15:0] Output
);

  wire [15:0] AR_t, PC_t;

  Convert_12_To_16 convert_12_to_16_1 (.in_1(AR), .out_2(AR_t));
  Convert_12_To_16 convert_12_to_16_2 (.in_1(PC), .out_2(PC_t));
  Multiplexer #(.select(3), .width(16)) multiplexer_1 (
    .in0({16{1'b0}}), .in1(AR_t), .in2(PC_t), .in3(DR), .in4(AC), .in5(IR), .in6(TR), .in7(RAM),
    .out(Output), .sel(S));  // open: en
endmodule

module Convert_12_To_16 (
  input  [11:0] in_1,
  output [15:0] out_2
);


  assign out_2 = {4'b0000, in_1};
endmodule

module Convert_16_To_12 (
  input  [15:0] in_1,
  output [11:0] out_2
);


  assign out_2 = in_1[11:0];
endmodule

module Convert_16_to_8 (
  input  [15:0] in_1,
  output [7:0] out_2
);


  assign out_2 = in_1[7:0];
endmodule

module BUS_CTRL (
  input  I,
  input  R,
  input  p,
  input  [15:0] SCD,
  input  [7:0] IRD,
  input  [11:0] IRB,
  output [2:0] S
);

  wire AC, and_1_out, and_2_out, and_3_out, and_4_out, and_5_out, and_7_out, and_8_out, and_9_out, AR, DR,
       IR, not_1_out, not_2_out, not_3_out, or_1_out, PC, RAM, TR;

  not not_1 (not_1_out, R);
  not not_2 (not_2_out, IRD[7]);
  or or_1 (or_1_out, IRD[0], IRD[1], IRD[2], IRD[6]);
  and and_1 (and_1_out, SCD[4], IRD[4]);
  and and_2 (and_2_out, SCD[5], IRD[5]);
  and and_3 (and_3_out, IRD[5], SCD[4]);
  and and_4 (and_4_out, IRD[3], SCD[4]);
  and and_5 (and_5_out, p, IRB[10]);
  not not_3 (not_3_out, R);
  and and_6 (TR, R, SCD[0]);
  and and_7 (and_7_out, not_1_out, SCD[1]);
  and and_8 (and_8_out, not_2_out, SCD[3], I);
  and and_9 (and_9_out, or_1_out, SCD[4]);
  or or_2 (AR, and_1_out, and_2_out);
  or or_3 (PC, SCD[0], and_3_out);
  and and_10 (DR, IRD[6], SCD[6]);
  or or_4 (AC, and_4_out, and_5_out);
  and and_11 (IR, not_3_out, SCD[2]);
  or or_5 (RAM, and_7_out, and_8_out, and_9_out);
  Priority_Encoder priority_encoder_1 (
    .in0(1'b0), .in1(AR), .in2(PC), .in3(DR), .in4(AC), .in5(IR), .in6(TR), .in7(RAM), .out(S), .en_in(1'b1));  // open: gs, en_out

  // Other names for the same wires on the sheet: B10 = IRB[10]; D0 = IRD[0]; D1 = IRD[1]; D2 = IRD[2]; D3 = IRD[3];
  //   D4 = IRD[4]; D5 = IRD[5]; D6 = IRD[6]; D7 = IRD[7]; T0 = SCD[0]; T1 = SCD[1]; T2 = SCD[2]; T3 = SCD[3];
  //   T4 = SCD[4]; T5 = SCD[5]; T6 = SCD[6]
endmodule

module R (
  input  [15:0] SCD,
  input  Clock,
  input  FGI,
  input  FGO,
  input  IEN,
  output R
);

  wire _0, _1, or_1_out;

  or or_1 (or_1_out, FGI, FGO);
  and and_1 (_0, R, SCD[2]);
  and and_2 (_1, ~SCD[0], ~SCD[1], ~SCD[2], IEN, or_1_out);  // AND_Gate
  S_R_Flip_Flop s_r_ff_1 (.S(_1), .clk(Clock), .R(_0), .Q(R));  // open: Qn, preset, reset, en

  // Other names for the same wires on the sheet: T0 = SCD[0]; T1 = SCD[1]; T2 = SCD[2]
endmodule

module FGI (
  input  p,
  input  Clock,
  input  [11:0] IRB,
  input  _1,
  output FGI
);

  wire _0;

  and and_1 (_0, p, IRB[11]);
  S_R_Flip_Flop s_r_ff_1 (.clk(Clock), .R(_0), .Q(FGI), .preset(_1));  // open: S, Qn, reset, en

  // Other names for the same wires on the sheet: B11 = IRB[11]
endmodule

module FGO (
  input  p,
  input  Clock,
  input  [11:0] IRB,
  input  _1,
  output FGO
);

  wire _0;

  and and_1 (_0, p, IRB[10]);
  S_R_Flip_Flop s_r_ff_1 (.clk(Clock), .R(_0), .Q(FGO), .preset(_1));  // open: S, Qn, reset, en

  // Other names for the same wires on the sheet: B10 = IRB[10]
endmodule

module IEN (
  input  R,
  input  p,
  input  [11:0] IRB,
  input  Clock,
  input  [15:0] SCD,
  output IEN
);

  wire _0, _1, and_1_out, and_2_out, B6, B7;

  and and_1 (and_1_out, p, B6);
  and and_2 (and_2_out, R, SCD[2]);
  and and_3 (_1, p, B7);
  or or_1 (_0, and_1_out, and_2_out);
  S_R_Flip_Flop s_r_ff_1 (.S(_1), .clk(Clock), .R(_0), .Q(IEN));  // open: Qn, preset, reset, en

  // Other names for the same wires on the sheet: B10 = IRB[10]; T2 = SCD[2]
endmodule

module Start (
  input  r,
  input  [11:0] IRB,
  input  Clock,
  output Start
);

  wire _0;

  and and_1 (_0, r, IRB[0]);
  S_R_Flip_Flop s_r_ff_1 (.S(_0), .clk(Clock), .R(1'b0), .Qn(Start));  // open: Q, preset, reset, en

  // Other names for the same wires on the sheet: B0 = IRB[0]
endmodule

module SCD (
  input  R,
  input  p,
  input  [7:0] IRD,
  input  r_2,
  input  Start,
  input  CLK,
  output [15:0] SCD
);

  wire and_1_out, and_2_out, and_3_out, and_4_out, and_5_out, CLR, or_1_out;
  wire [3:0] SC;

  or or_1 (or_1_out, IRD[0], IRD[1], IRD[2], IRD[5]);
  and and_1 (and_1_out, R, SCD[2]);
  and and_2 (and_2_out, or_1_out, SCD[5]);
  and and_3 (and_3_out, IRD[3], SCD[4]);
  and and_4 (and_4_out, SCD[4], IRD[4]);
  and and_5 (and_5_out, IRD[6], SCD[6]);
  Counter_4_Bit counter_4_bit_1 (.Start(Start), .CLK(CLK), .CLR(CLR), .Out(SC));
  or or_2 (CLR, and_1_out, and_2_out, and_3_out, and_4_out, p, and_5_out, r_2);
  Decoder #(.select(4), .enable("false")) decoder_1 (
    .out0(SCD[0]), .out1(SCD[1]), .out2(SCD[2]), .out3(SCD[3]), .out4(SCD[4]), .out5(SCD[5]), .out6(SCD[6]),
    .out7(SCD[7]), .out8(SCD[8]), .out9(SCD[9]), .out10(SCD[10]), .out11(SCD[11]), .out12(SCD[12]),
    .out13(SCD[13]), .out14(SCD[14]), .out15(SCD[15]), .sel(SC));

  // Other names for the same wires on the sheet: D0 = IRD[0]; D1 = IRD[1]; D2 = IRD[2]; D3 = IRD[3]; D4 = IRD[4];
  //   D5 = IRD[5]; D6 = IRD[6]; T2 = SCD[2]; T4 = SCD[4]; T5 = SCD[5]; T6 = SCD[6]
endmodule

module Options (
  input  [15:0] IR,
  input  [15:0] SCD,
  output [11:0] IRB,
  output [7:0] IRD,
  output I,
  output r,
  output p
);

  wire and_1_out, not_1_out;

  and and_1 (and_1_out, SCD[3], IRD[7]);
  not not_1 (not_1_out, IR[15]);
  and and_2 (r, not_1_out, and_1_out);
  and and_3 (p, IR[15], and_1_out);
  Decoder #(.select(3), .enable("false")) decoder_1 (
    .out0(IRD[0]), .out1(IRD[1]), .out2(IRD[2]), .out3(IRD[3]), .out4(IRD[4]), .out5(IRD[5]), .out6(IRD[6]),
    .out7(IRD[7]), .sel(IR[14:12]));

  assign I = IR[15];
  assign IRB = IR[11:0];

  // Other names for the same wires on the sheet: D7 = IRD[7]; T3 = SCD[3]
endmodule

module E (
  input  r,
  input  E_Out,
  input  [7:0] IRD,
  input  [15:0] SCD,
  input  CLK,
  input  [11:0] IRB,
  input  [15:0] AC,
  output E
);

  wire ADD, CIL, CIR, CLE, CME, E_Not, En, multiplexer_1_out;
  wire [2:0] priority_encoder_1_out;

  and and_1 (ADD, IRD[1], SCD[5]);
  and and_2 (CLE, r, IRB[10]);
  and and_3 (CME, r, IRB[8]);
  and and_4 (CIR, r, IRB[7]);
  and and_5 (CIL, r, IRB[6]);
  Priority_Encoder priority_encoder_1 (
    .in0(ADD), .in1(CLE), .in2(CME), .in3(CIR), .in4(CIL), .out(priority_encoder_1_out), .gs(En));  // open: in5, in6, in7, en_in, en_out
  Multiplexer #(.select(3)) multiplexer_1 (
    .in0(E_Out), .in1(1'b0), .in2(E_Not), .in3(AC[0]), .in4(AC[15]), .out(multiplexer_1_out),
    .sel(priority_encoder_1_out), .en(En));  // open: in5, in6, in7
  D_Flip_Flop d_ff_1 (.clk(CLK), .D(multiplexer_1_out), .Q(E), .Qn(E_Not), .en(En));  // open: preset, reset

  // Other names for the same wires on the sheet: B1 = IRB[0]; B6 = IRB[6]; B7 = IRB[7]; B8 = IRB[8]; B10 = IRB[10];
  //   D1 = IRD[1]; T5 = SCD[5]
endmodule

module Counter_4_Bit (
  input  CLR,
  input  Start,
  input  CLK,
  output [3:0] Out
);

  wire and_1_out, not_1_out;

  not not_1 (not_1_out, CLR);
  and and_1 (and_1_out, not_1_out, Start);
  Counter #(.width(4), .max('hf)) counter_1 (
    .load(CLR), .D(4'b0000), .count(and_1_out), .Q(Out), .clk(CLK));  // open: carry, clr
endmodule
